# Fritzing sketch IR_LED (saved by Fritzing 0.9.3b)
breadboards: 1

parts:
  Raspberry_Pi1 = Raspberry Pi 2
  R6 = Resistor [tolerance=±5% resistance=220 package=THT]
  LED1 = LED - 5mm [color="Infrared (880nm)" package="5 mm [THT]"]
  R7 = Resistor [tolerance=±5% resistance=220 package=THT]
  Q1 = NPN-Transistor [package="TO92 [THT]"]

nets:
  N1: Raspberry_Pi1.3v3, R7.Pin_1
  N2: Raspberry_Pi1.GPIO17, R6.Pin_1
  N3: Raspberry_Pi1.GND, Q1.C
  N4: R6.Pin_0, Q1.B
  N5: LED1.cathode, R7.Pin_0
  N6: LED1.anode, Q1.E
