# Fritzing sketch TSOP4838 (saved by Fritzing 0.9.3b)
breadboards: 1

parts:
  Raspberry_Pi1 = Raspberry Pi 2
  TSOP4838 = TSOP312.., 314.. [package=THT]
  R6 = Resistor [tolerance=±5% resistance=330 package=THT]
  LED1 = LED - 5mm [color="Yellow (595nm)" package="5 mm [THT]"]

nets:
  N1: Raspberry_Pi1.3v3, TSOP4838.Data, LED1.cathode
  N2: Raspberry_Pi1.GND, TSOP4838.Vs
  N3: Raspberry_Pi1.GPIO18, TSOP4838.GND, R6.Pin_1
  N4: R6.Pin_0, LED1.anode
